# Fritzing sketch DualHeatStage---Breadboard-Version (saved by Fritzing 0.9.2b)
circuit board: 8.46667cm x 5.64444cm
breadboards: 1

parts:
  Raspberry_Pi1 = Raspberry Pi 2
  THERMO1 = MAX31855 Breakout Board with Thermocouple
  THERMO2 = MAX31855 Breakout Board with Thermocouple
  Q1 = Basic FET N-Channel [package="DPak [SMD]"]
  Q2 = Basic FET N-Channel [package="TO220 [THT]"]
  J1 = Peltier Element
  JACK1 = 2.1mm DC Barrel Jack
  JACK2 = 2.1mm DC Barrel Jack
  Q3 = Basic FET N-Channel [package="TO220 [THT]"]
  JACK3 = 2.1mm Barrel Jack with Terminal Block

nets:
  3V3: Raspberry_Pi1.3v3, Raspberry_Pi1.3V3, THERMO1.Vin, THERMO2.Vin
  N1: Raspberry_Pi1.GPIO17, Q1.Gate
  N2: Raspberry_Pi1.GPIO27, Q2.gate
  N3: Raspberry_Pi1.GPIO22, Q3.gate
  N4: Raspberry_Pi1.GPIO13, THERMO1.DO
  N5: Raspberry_Pi1.GPIO19, THERMO1.CS
  N6: Raspberry_Pi1.GPIO26, THERMO1.CLK
  GND: Raspberry_Pi1.GND, THERMO1.GND, THERMO2.GND, Q1.drain, Q1.source, Q2.source, J1.pin1, JACK1.switch, JACK2.switch, Q3.source
  N7: Raspberry_Pi1.GPIO21, THERMO2.CLK
  N8: Raspberry_Pi1.GPIO20, THERMO2.CS
  N9: Raspberry_Pi1.GPIO16, THERMO2.DO
  N10: Q2.drain, JACK3.NEG
  N11: J1.pin2, JACK2.center
  N12: JACK1.center, JACK3.POS

custom parts:
  2.1mm DC Barrel Jack: 2.1mm DC Barrel Jack with Thru-Hole Connectors (breadboardable)
